# Fritzing sketch Ringtone Doorbell (saved by Fritzing 0.9.0b)
breadboards: 1

parts:
  TRINKET1 = Trinket 5V
  J1 = Piezo Speaker
  BUTTON1 = Arcade Button (pink)
  BATT1 = 3xAAA Switchable Battery Pack w/Bare Wire
  R3 = Resistor [tolerance=±5% resistance=470 package=THT]
  R4 = Resistor [tolerance=±5% resistance=10k package=THT]

nets:
  N1: TRINKET1.no_name_yet#2, J1.pin1, BUTTON1.no_name_yet#2, BATT1.NEG
  N2: TRINKET1.no_name_yet#8, R3.Pin_0
  N3: TRINKET1.no_name_yet#9, BUTTON1.no_name_yet#1, R4.Pin_1
  N4: J1.pin2, R3.Pin_1
  N5: BATT1.POS, R4.Pin_0

custom parts:
  Trinket 5V: Adafruit Trinket 5V
  Arcade Button (pink): Adafruit Arcade Button (pink)
  3xAAA Switchable Battery Pack w/Bare Wire: 3xAAA Switchable Battery Pack w/Bare Wire Connectors
